# Fritzing sketch DuckHuntFritzing (saved by Fritzing 0.9.3b)

parts:
  Composant1 = Arduino Ethernet Shield (Rev3)
  SP1 = SPEAKER [package=pcb_mount_speaker]
  U2 = JOYSTICK-PSP1000 [package=joystick-psp1000]
  S1 = SWITCH-MOMENTARY-2 [package=tactile_switch_tall]

nets:
  N1: Composant1.D2, S1.2
  N2: Composant1.PWM_D3, SP1.-
  5V: Composant1.5V, U2.VCC
  GND: Composant1.GND, U2.GND
  N3: Composant1.A4/SDA, U2.Y
  N4: Composant1.A5/SCL, U2.X
